# Fritzing sketch SmartThings Lock (saved by Fritzing 0.9.1b)
breadboards: 1

parts:
  Part1 = Arduino Uno (Rev3)
  PIR1 = PIR sensor
  J1 = Piezo Speaker

nets:
  N1: Part1.D11_PWM/MOSI, PIR1.SIG
  GND: Part1.GND, PIR1.GND, J1.pin1
  N2: Part1.D6_PWM, J1.pin2
  5V: Part1.5V, PIR1.VDD
